# Fritzing sketch counter_breadboard (saved by Fritzing 0.9.2b)
breadboards: 1

parts:
  Part1 = Photon
  R1 = Resistor [tolerance=±5% resistance=220 package=THT]
  R2 = Rotary Potentiometer (Small) [maximum_resistance=100kΩ package=THT]
  LED1 = LED - 5mm [color="Red (633nm)" package="5 mm [THT]"]

nets:
  N1: Part1.A0, R2.wiper
  N2: Part1.GND, R2.leg1, LED1.anode
  N3: Part1.D7, R1.Pin_0
  N4: Part1.VBAT, R2.leg2
  N5: R1.Pin_1, LED1.cathode
